# Fritzing sketch Pico 7 segment reordered bits (saved by Fritzing 0.9.6b)
breadboards: 1

parts:
  Mod1 = Raspberry Pi Pico
  Q1 = NPN-Transistor [package="TO92 [THT]"]
  R1 = Resistor [tolerance=±5% power=0.25 resistance=220 package=THT]
  R2 = Resistor [tolerance=±5% power=0.25 resistance=220 package=THT]
  Q3 = NPN-Transistor [package="TO92 [THT]"]
  Q5 = NPN-Transistor [package="TO92 [THT]"]
  Q7 = NPN-Transistor [package="TO92 [THT]"]
  Q8 = NPN-Transistor [package="TO92 [THT]"]
  Q9 = PNP-Transistor [package="TO92 [THT]"]
  Q10 = PNP-Transistor [package="TO92 [THT]"]
  Q11 = PNP-Transistor [package="TO92 [THT]"]
  Q12 = PNP-Transistor [package="TO92 [THT]"]
  R3 = Resistor [tolerance=±5% power=0.25 resistance=220 package=THT]
  R4 = Resistor [tolerance=±5% power=0.25 resistance=220 package=THT]
  R8 = Resistor [tolerance=±5% power=0.25 resistance=220 package=THT]
  R9 = Resistor [tolerance=±5% power=0.25 resistance=220 package=THT]
  R11 = Resistor [tolerance=±5% power=0.25 resistance=220 package=THT]
  R12 = Resistor [tolerance=±5% power=0.25 resistance=220 package=THT]
  R14 = Resistor [tolerance=±5% power=0.25 resistance=220 package=THT]
  R16 = Resistor [tolerance=±5% power=0.25 resistance=220 package=THT]
  R18 = Resistor [tolerance=±5% power=0.25 resistance=220 package=THT]
  R19 = Resistor [tolerance=±5% power=0.25 resistance=220 package=THT]
  R20 = Resistor [tolerance=±5% power=0.25 resistance=220 package=THT]
  R21 = Resistor [tolerance=±5% power=0.25 resistance=220 package=THT]
  LED2 = 7-SEGMENT-4DIGIT-YOUNGSUN [package=7-segment-4digit-youngsun-longpads]
  R22 = Resistor [tolerance=±5% power=0.25 resistance=220 package=THT]
  R23 = Resistor [tolerance=±5% power=0.25 resistance=220 package=THT]
  Q13 = NPN-Transistor [package="TO92 [THT]"]
  R24 = Resistor [tolerance=±5% power=0.25 resistance=220 package=THT]
  Q14 = NPN-Transistor [package="TO92 [THT]"]
  Q15 = NPN-Transistor [package="TO92 [THT]"]
  R25 = Resistor [tolerance=±5% power=0.25 resistance=220 package=THT]
  R26 = Resistor [tolerance=±5% power=0.25 resistance=220 package=THT]
  R15 = Resistor [tolerance=±5% power=0.25 resistance=220 package=THT]

nets:
  N1: Mod1.pin_3, Mod1.pin_8, Mod1.pin_13, Mod1.pin_18, Mod1.pin_23, Mod1.pin_28, Mod1.pin_33, Mod1.pin_38, Mod1.pin_42, Q1.E, Q3.E, Q5.E, Q7.E, Q8.E, Q13.E, Q14.E, Q15.E
  N2: Mod1.pin_11, R15.Pin_0
  N3: Mod1.pin_12, R14.Pin_0
  N4: Mod1.pin_14, R12.Pin_0
  N5: Mod1.pin_15, R11.Pin_0
  N6: Mod1.pin_16, R8.Pin_0
  N7: Mod1.pin_17, R23.Pin_0
  N8: Mod1.pin_19, R4.Pin_0
  N9: Mod1.pin_20, R1.Pin_0
  N10: Mod1.pin_21, R21.Pin_1
  N11: Mod1.pin_22, R20.Pin_1
  N12: Mod1.pin_24, R19.Pin_1
  N13: Mod1.pin_25, R18.Pin_1
  N14: Mod1.pin_36, Q9.E, Q10.E, Q11.E, Q12.E
  N15: Q1.B, R1.Pin_1
  N16: Q1.C, R2.Pin_1
  N17: R2.Pin_0, LED2.E
  N18: Q3.B, R23.Pin_1
  N19: Q3.C, R22.Pin_1
  N20: Q5.B, R8.Pin_1
  N21: Q5.C, R24.Pin_1
  N22: Q7.B, R14.Pin_1
  N23: Q7.C, R26.Pin_1
  N24: Q8.B, R15.Pin_1
  N25: Q8.C, R16.Pin_1
  N26: Q9.B, R20.Pin_0
  N27: Q9.C, LED2.DIG3
  N28: Q10.B, R19.Pin_0
  N29: Q10.C, LED2.DIG2
  N30: Q11.B, R21.Pin_0
  N31: Q11.C, LED2.DIG4
  N32: Q12.B, R18.Pin_0
  N33: Q12.C, LED2.DIG1
  N34: R3.Pin_0, LED2.D
  N35: R3.Pin_1, Q13.C
  N36: R4.Pin_1, Q13.B
  N37: R9.Pin_0, LED2.A
  N38: R9.Pin_1, Q14.C
  N39: R11.Pin_1, Q14.B
  N40: R12.Pin_1, Q15.B
  N41: R16.Pin_0, LED2.DP
  N42: LED2.F, R26.Pin_0
  N43: LED2.C, R25.Pin_0
  N44: LED2.G, R24.Pin_0
  N45: LED2.B, R22.Pin_0
  N46: Q15.C, R25.Pin_1

notes:
  A
  G
  B
  D
  E
  C
  F
  dp
  4
  3
  2
  1

custom parts:
  Raspberry Pi Pico: Raspberry Pi Pico. Based around the RP2040 microcontroller the Pico is a low cost microcontroller device bringing Raspberry Pi quality, cost, and easy of use to the microcontroller space. Jan 2021, Split part in to two versions: tht (this one) and SMD. This one will drill holes for a .1 in header in pcb to allow plugging in the module as well as providing pads to solder the module to the top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
  7-SEGMENT-4DIGIT-YOUNGSUN: This is a part for the 4-Digit 7-segment LEDs from Young Sun. Different from the Digikey LEDs, all 16 pins are used. The LONGPADS Variant is used for a test jig, but you may like it because there is more pad to solder to. If you are concerned about routing space, the standard works just fine though.
