# Fritzing sketch seven-segment-wiring (saved by Fritzing 0.9.6b)
breadboards: 1

parts:
  Mod1 = Raspberry Pi Pico
  R1 = Resistor [tolerance=±5% power=0.25 resistance=220 package=THT]
  R2 = Resistor [tolerance=±5% power=0.25 resistance=220 package=THT]
  R3 = Resistor [tolerance=±5% power=0.25 resistance=220 package=THT]
  R4 = Resistor [tolerance=±5% power=0.25 resistance=220 package=THT]
  R5 = Resistor [tolerance=±5% power=0.25 resistance=220 package=THT]
  R6 = Resistor [tolerance=±5% power=0.25 resistance=220 package=THT]
  R7 = Resistor [tolerance=±5% power=0.25 resistance=220 package=THT]
  R8 = Resistor [tolerance=±5% power=0.25 resistance=220 package=THT]
  Q2 = PNP-Transistor [package="TO92 [THT]"]
  Q3 = PNP-Transistor [package="TO92 [THT]"]
  U1 = 7-SEGMENT-4DIGIT [package=7-segment-4digit]
  Q4 = PNP-Transistor [package="TO92 [THT]"]
  Q1 = PNP-Transistor [package="TO92 [THT]"]

nets:
  N1: Mod1.pin_3, Mod1.pin_8, Mod1.pin_13, Mod1.pin_18, Mod1.pin_23, Mod1.pin_28, Mod1.pin_33, Mod1.pin_38, Q2.C, Q3.C, Q4.C, Q1.C
  N2: Mod1.pin_11, R4.Pin_0
  N3: Mod1.pin_12, R1.Pin_0
  N4: Mod1.pin_14, R5.Pin_0
  N5: Mod1.pin_15, R6.Pin_0
  N6: Mod1.pin_16, R7.Pin_0
  N7: Mod1.pin_17, R8.Pin_0
  N8: Mod1.pin_19, R2.Pin_0
  N9: Mod1.pin_20, R3.Pin_0
  N10: Mod1.pin_21, Q1.B
  N11: Mod1.pin_22, Q3.B
  N12: Mod1.pin_24, Q2.B
  N13: Mod1.pin_25, Q4.B
  N14: R1.Pin_1, U1.7
  N15: R2.Pin_1, U1.2
  N16: R3.Pin_1, U1.1
  N17: R4.Pin_1, U1.8
  N18: R5.Pin_1, U1.6
  N19: R6.Pin_1, U1.5
  N20: R7.Pin_1, U1.4
  N21: R8.Pin_1, U1.3
  N22: Q2.E, U1.15
  N23: Q3.E, U1.14
  N24: U1.13, Q1.E
  N25: U1.16, Q4.E

custom parts:
  Raspberry Pi Pico: Raspberry Pi Pico. Based around the RP2040 microcontroller the Pico is a low cost microcontroller device bringing Raspberry Pi quality, cost, and easy of use to the microcontroller space. Jan 2021, Split part in to two versions: tht (this one) and SMD. This one will drill holes for a .1 in header in pcb to allow plugging in the module as well as providing pads to solder the module to the top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
